// Digital circuit lab2_part1.dig as structural Verilog
module lab2_part1 (
  input  [3:0] inA_0,
  input  [3:0] inA_1,
  input  [3:0] inA_2,
  input  [3:0] inA_3,
  input  [3:0] inB_0,
  input  [3:0] inB_1,
  input  [3:0] inB_2,
  input  [3:0] inB_3,
  input  [3:0] A,
  input  [3:0] B,
  output [3:0] out0,
  output [3:0] out1,
  output [3:0] out2,
  output [3:0] out3,
  output [3:0] out
);

  Multiplexer #(.Bits(4)) multiplexer_1 (.in_0(A), .in_1(B), .out(out));  // open: sel
  // Pins of 1 and 4 bits meet at A
  // Pins of 1 and 4 bits meet at B
  // Pins of 1 and 4 bits meet at out

  assign inA_0 = A;
  assign inA_1 = A;
  assign inA_2 = A;
  assign inA_3 = A;
  assign inB_0 = B;
  assign inB_1 = B;
  assign inB_2 = B;
  assign inB_3 = B;
  assign out0 = out;
  assign out1 = out;
  assign out2 = out;
  assign out3 = out;

  // Notes on the sheet:
  //   Interface (do not edit the content inside this box)
  //   Inputs
  //   Outputs
  //   Rotatee:
  //   Rotation amount:
  //   Result of Rotating  input A by the amount given by input B:
endmodule

/* Test case:
inA_3 inA_2 inA_1 inA_0 inB_1 inB_0  out3 out2 out1 out0
 0     0     0     0     0     0      0    0    0    0  
 0     0     0     1     0     0      0    0    0    1  
 0     0     0     1     0     1      0    0    1    0  
 0     0     0     1     1     0      0    1    0    0  
 0     0     0     1     1     1      1    0    0    0   
 0     1     0     1     0     0      0    1    0    1  
 0     1     0     1     0     1      1    0    1    0  
 0     1     0     1     1     0      0    1    0    1  
 0     1     0     1     1     1      1    0    1    0   
*/
