// Digital circuit lab2_part3.dig as structural Verilog
module lab2_part3 (
  input  clk,
  input  in0,
  input  in1,
  input  in2,
  input  in3,
  input  sel_write_1,
  input  sel_write_0,
  input  sel_readA_1,
  input  sel_readA_0,
  input  sel_readB_1,
  input  sel_readB_0,
  input  inA_0_2,
  input  inA_1_2,
  input  inA_2_2,
  input  inA_3_2,
  input  inB_0_2,
  input  inB_1_2,
  input  inB_2_2,
  input  inB_3_2,
  output out0,
  output out1,
  output out2,
  output out3,
  output reg0_0,
  output reg0_1,
  output reg0_2,
  output reg0_3,
  output reg1_0,
  output reg1_1,
  output reg1_2,
  output reg1_3,
  output reg2_0,
  output reg2_1,
  output reg2_2,
  output reg2_3,
  output reg3_0,
  output reg3_1,
  output reg3_2,
  output reg3_3,
  output inA_0,
  output inA_1,
  output inA_2,
  output inA_3,
  output inB_0,
  output inB_1,
  output inB_2,
  output inB_3,
  output out4,
  output out5,
  output out6,
  output out7
);

  wire undriven, undriven_2, undriven_3, undriven_4;

  Seven_Seg_Hex seven_seg_hex_1 (.d({inA_3_2, inA_2_2, inA_1_2, inA_0_2}), .dp(1'b0));
  Seven_Seg_Hex seven_seg_hex_2 (.d({reg3_3, reg3_2, reg3_1, reg3_0}), .dp(1'b0));
  Seven_Seg_Hex seven_seg_hex_3 (.d({in3, in2, in1, in0}), .dp(1'b0));
  Multiplexer #(.Selector_Bits(2)) multiplexer_1 (
    .sel({inB_1_2, inB_0_2}), .in_0(inA_0_2), .in_1(inA_1_2), .in_2(inA_2_2), .in_3(inA_3_2), .out(out0));
  Multiplexer #(.Selector_Bits(2)) multiplexer_2 (
    .sel({inB_1_2, inB_0_2}), .in_0(inA_1_2), .in_1(inA_0_2), .in_2(inA_3_2), .in_3(inA_2_2), .out(out1));
  Multiplexer #(.Selector_Bits(2)) multiplexer_3 (
    .sel({inB_1_2, inB_0_2}), .in_0(inA_2_2), .in_1(inA_3_2), .in_2(inA_0_2), .in_3(inA_1_2), .out(out2));
  Multiplexer #(.Selector_Bits(2)) multiplexer_4 (
    .sel({inB_1_2, inB_0_2}), .in_0(inA_3_2), .in_1(inA_2_2), .in_2(inA_1_2), .in_3(inA_0_2), .out(out3));
  Seven_Seg_Hex seven_seg_hex_4 (.d({inB_3_2, inB_2_2, inB_1_2, inB_0_2}), .dp(1'b0));
  Seven_Seg_Hex seven_seg_hex_5 (.d({reg2_3, reg2_2, reg2_1, reg2_0}), .dp(1'b0));
  Seven_Seg_Hex seven_seg_hex_6 (.d({2'b00, sel_write_1, sel_write_0}), .dp(1'b0));
  Seven_Seg_Hex seven_seg_hex_7 (.d({2'b00, sel_readA_1, sel_readA_0}), .dp(1'b0));
  Seven_Seg_Hex seven_seg_hex_8 (.d({out3, out2, out1, out0}), .dp(1'b0));
  Seven_Seg_Hex seven_seg_hex_9 (.d({reg1_3, reg1_2, reg1_1, reg1_0}), .dp(1'b0));
  Seven_Seg_Hex seven_seg_hex_10 (.d({2'b00, sel_readB_1, sel_readB_0}), .dp(1'b0));
  Seven_Seg_Hex seven_seg_hex_11 (.d({reg0_3, reg0_2, reg0_1, reg0_0}), .dp(1'b0));
  Decoder decoder_1 (.sel(undriven), .out_0(sel_write_1), .out_1(sel_write_0));
  Register #(.Bits(4)) register_1 (
    .D({in3, in2, in1, in0}), .C(clk), .en(undriven), .Q({reg0_3, reg0_2, reg0_1, reg0_0}));
  Multiplexer #(.Selector_Bits(2)) multiplexer_5 (
    .sel({sel_readA_1, sel_readA_0}), .in_0(reg0_0), .in_1(reg1_0), .in_2(reg2_0), .in_3(reg3_0));  // open: out
  Decoder decoder_2 (.sel(undriven_2), .out_0(sel_write_1), .out_1(sel_write_0));
  Register #(.Bits(4)) register_2 (
    .D({in3, in2, in1, in0}), .C(clk), .en(undriven_2), .Q({reg1_3, reg1_2, reg1_1, reg1_0}));
  Decoder decoder_3 (.sel(undriven_3), .out_0(sel_write_1), .out_1(sel_write_0));
  Register #(.Bits(4)) register_3 (
    .D({in3, in2, in1, in0}), .C(clk), .en(undriven_3), .Q({reg2_3, reg2_2, reg2_1, reg2_0}));
  Multiplexer #(.Selector_Bits(2)) multiplexer_6 (
    .sel({sel_readB_1, sel_readB_0}), .in_0(reg0_0), .in_1(reg1_0), .in_2(reg2_0), .in_3(reg3_0));  // open: out
  Decoder decoder_4 (.sel(undriven_4), .out_0(sel_write_1), .out_1(sel_write_0));
  Register #(.Bits(4)) register_4 (
    .D({in3, in2, in1, in0}), .C(clk), .en(undriven_4), .Q({reg3_3, reg3_2, reg3_1, reg3_0}));
  // Pins of 1 and 4 bits meet at {reg0_3, reg0_2, reg0_1, reg0_0}
  // Pins of 1 and 4 bits meet at {reg1_3, reg1_2, reg1_1, reg1_0}
  // Pins of 1 and 4 bits meet at {reg2_3, reg2_2, reg2_1, reg2_0}
  // Pins of 1 and 4 bits meet at {reg3_3, reg3_2, reg3_1, reg3_0}
  // Pins of 1 and 4 bits meet at {reg0_3, reg0_2, reg0_1, reg0_0}
  // Pins of 1 and 4 bits meet at {reg1_3, reg1_2, reg1_1, reg1_0}
  // Pins of 1 and 4 bits meet at {reg2_3, reg2_2, reg2_1, reg2_0}
  // Pins of 1 and 4 bits meet at {reg3_3, reg3_2, reg3_1, reg3_0}

  assign inA_0 = inA_0_2;
  assign inA_1 = inA_1_2;
  assign inA_2 = inA_2_2;
  assign inA_3 = inA_3_2;
  assign inB_0 = inB_0_2;
  assign inB_1 = inB_1_2;
  assign inB_2 = inB_2_2;
  assign inB_3 = inB_3_2;
  assign out4 = out0;
  assign out5 = out1;
  assign out6 = out2;
  assign out7 = out3;

  // Notes on the sheet:
  //   From part 1
  //   Interface (do not edit the content inside this box)
  //   Inputs
  //   Keypad
  //   Outputs
  //   Registers
  //   Values read into ALU inputs
  //   Rotatee
  //   Register 3
  //   Synchronizing Clock
  //   Rotation amount:
  //   Register Selection: Write-to
  //   Rotatee:
  //   Result of Rotating  input A by the amount given by input B:
  //   Register 2
  //   Register Selection: Read-from
  //   ALU Output
  //   ALU input A register address:
  //   Register 1
  //   ALU input B register address:
  //   Register 0
endmodule

/* Test case:
clk in3 in2 in1 in0 sel^write_1 sel^write_0 sel^readA_1 sel^readA_0 sel^readB_1 sel^readB_0  reg3_3 reg3_2 reg3_1 reg3_0 reg2_3 reg2_2 reg2_1 reg2_0 reg1_3 reg1_2 reg1_1 reg1_0 reg0_3 reg0_2 reg0_1 reg0_0 out3 out2 out1 out0
 0   0   0   0   0   0           0           0           0           0           0            0      0      0      0      0      0      0      0      0      0      0      0      0      0      0      0      0    0    0    0
 1   0   0   0   0   0           0           0           0           0           0            0      0      0      0      0      0      0      0      0      0      0      0      0      0      0      0      0    0    0    0
 0   0   1   0   1   1           1           0           0           0           0            0      0      0      0      0      0      0      0      0      0      0      0      0      0      0      0      0    0    0    0
 1   0   1   0   1   1           1           0           0           0           0            0      1      0      1      0      0      0      0      0      0      0      0      0      0      0      0      0    0    0    0
 0   0   0   0   1   0           1           0           0           0           0            0      1      0      1      0      0      0      0      0      0      0      0      0      0      0      0      0    0    0    0
 1   0   0   0   1   0           1           0           0           0           0            0      1      0      1      0      0      0      0      0      0      0      1      0      0      0      0      0    0    0    0
 0   0   0   0   0   0           0           1           1           0           1            0      1      0      1      0      0      0      0      0      0      0      1      0      0      0      0      1    0    1    0
 1   0   0   0   0   0           0           1           1           0           1            0      1      0      1      0      0      0      0      0      0      0      1      0      0      0      0      1    0    1    0
 0   0   0   0   0   0           0           0           1           1           1            0      1      0      1      0      0      0      0      0      0      0      1      0      0      0      0      0    0    1    0
 1   0   0   0   0   0           0           0           1           1           1            0      1      0      1      0      0      0      0      0      0      0      1      0      0      0      0      0    0    1    0
*/
